# Fritzing sketch Esquema_Fritzing (saved by Fritzing 0.9.4)

parts:
  S1 = H-Bridge with L298N
  M1 = DC Motor
  M2 = DC Motor
  Componente1 = Arduino Uno (Rev3)
  Componente2 = Bluetooth HC-05 Macho
  M3 = DC Motor
  M4 = DC Motor
  VCC1 = 4 x AAA Battery Mount

nets:
  N1: S1.12V, VCC1.+
  GND: S1.GND, Componente1.GND, Componente2.GND, VCC1.-
  5V: S1.5V, Componente1.VIN
  N2: S1.IN1, Componente1.D13/SCK
  N3: S1.IN2, Componente1.D12/MISO
  N4: S1.IN3, Componente1.D11_PWM/MOSI
  N5: S1.IN4, Componente1.D10_PWM/SS
  N6: S1.M1-01, M1.pin_1, M3.pin_1
  N7: S1.M1-02, M1.pin_2, M3.pin_2
  N8: S1.M2-01, M2.pin_1
  N9: S1.M2-02, M2.pin_2, M4.pin_2
  N10: Componente1.D0/RX, Componente2.TXD
  N11: Componente1.D1/TX, Componente2.RXD
  3V3: Componente1.3V3, Componente2.VCC

custom parts:
  H-Bridge with L298N: h-bridge
